# Fritzing sketch Circuit_Diagram (saved by Fritzing 1.0.0rc)

parts:
  Mod1 = Raspberry Pi Pico W
  Part1 = RFID-RC522-v3
  GREEN_LED = smd LED [color="Green (555nm)" package="0603 [SMD]"]
  RED_LED = smd LED [color="Red (633nm)" package="0603 [SMD]"]
  J1 = Basic Servo
  IC1 = Voltage Regulator [package=78xxl]
  S1 = Taiway 100-SP-X-T1 SPDT Miniature Toggle Switch [part_number=100-SP-X-T1-0-0-B1-M2 package=THT]
  C1 = Capacitor [package=cap-pth-small2]
  C2 = Capacitor [package=cap-pth-small2]
  R2 = Resistor [tolerance=±5% resistance=68 package="2010 [SMD]"]
  R1 = Resistor [tolerance=±5% resistance=68 package="2010 [SMD]"]
  J2 = Piezo Speaker
  JACK2 = 2.1mm DC Barrel Jack

nets:
  GND: Mod1.pin_3, Mod1.pin_33, Mod1.pin_38, Mod1.pin_42, Part1.GND, GREEN_LED.cathode, RED_LED.cathode, J1.gnd, J2.pin1
  N1: Mod1.pin_9, R2.Pin_1
  N2: Mod1.pin_10, R1.Pin_1
  N3: Mod1.pin_11, J2.pin2
  N4: Mod1.pin_12, J1.pulse
  N5: Mod1.pin_14, Part1.RST
  N6: Mod1.pin_21, Part1.MISO
  N7: Mod1.pin_22, Part1.SDA
  N8: Mod1.pin_24, Part1.SCK
  N9: Mod1.pin_25, Part1.MOSI
  3.3V: Mod1.pin_36, Part1.3.3V, J1.vcc
  N10: Mod1.pin_40, S1.L2
  N11: GREEN_LED.anode, R2.Pin_0
  N12: RED_LED.anode, R1.Pin_0
  N13: IC1.GND, C1.2, C2.1, JACK2.switch
  N14: IC1.IN, C2.2, JACK2.center
  N15: IC1.OUT, S1.COM, C1.1

custom parts:
  Raspberry Pi Pico W: Raspberry Pi Pico W. Based around the RP2040 microcontroller the Pico W is a low cost microcontroller device bringing Raspberry Pi quality, cost, and easy of use to the microcontroller space. The areas marked KEEPOUT in pcb silkscreen should not have traces running through them to avoid shorts on a soldered in module!
  RFID-RC522-v3: A simple China made RFID-RC522 Reader (6x4 cm); do check the pin labels, as this is a MFRC522 based clone.
  2.1mm DC Barrel Jack: 2.1mm DC Barrel Jack with Thru-Hole Connectors (breadboardable)
